# Fritzing sketch schematics (saved by Fritzing 0.8.3b)
breadboards: 1

parts:
  Arduino1 = Arduino
  M2 = DC Motor
  M3 = DC Motor
  LED1 = LED - 5mm [color="Red (633nm)" package="5 mm [THT]"]
  LED2 = LED - 5mm [color="Red (633nm)" package="5 mm [THT]"]
  LED3 = LED - 5mm [color="White (6500K)" package="5 mm [THT]"]
  LED4 = LED - 5mm [color="White (6500K)" package="5 mm [THT]"]
  LED5 = LED - 5mm [color="Orange (620nm)" package="5 mm [THT]"]
  LED6 = LED - 5mm [color="Orange (620nm)" package="5 mm [THT]"]
  LED7 = LED - 5mm [color="Orange (620nm)" package="5 mm [THT]"]
  LED8 = LED - 5mm [color="Orange (620nm)" package="5 mm [THT]"]
  LED9 = LED - 5mm [color="Red (633nm)" package="5 mm [THT]"]
  LED10 = LED - 5mm [color="Red (633nm)" package="5 mm [THT]"]
  M1 = DC Motor
  M4 = DC Motor
  J1 = Infrared Proximity Sensor  # not connected
  J2 = Infrared Proximity Sensor  # not connected
  J3 = Infrared Proximity Sensor  # not connected
  Horn = Piezo Speaker
  Powerswitch = Toggle Switch [package=THT]
  VCC1 = 4 x AAA Battery Mount
  Shift_Register_for_LED_lights = 74HC595 [package="DIP16 [THT]"]
  Onderdeel2 = Arduino Motor Shield (Rev3)
  U1 = XBee
  Onderdeel3 = Arduino Wireless SD Shield
  C1 = Electrolytic Capacitor [capacitance=1mF package="100 mil [THT, electrolytic]"]  # not connected
  U2 = XBee

nets (from the schematic view):
  GND: Arduino1.GND, Horn.pin1, Shift_Register_for_LED_lights.GND
  +5V: Arduino1.+5V, Shift_Register_for_LED_lights.VCC
  N1: M2.pin_1, M3.pin_2, Onderdeel2.A+
  N2: M2.pin_2, M3.pin_1, Onderdeel2.A-
  N3: LED1.anode, LED2.cathode
  N4: LED3.anode, LED4.cathode
  N5: LED5.cathode, LED8.anode
  N6: LED6.cathode, LED7.anode
  N7: LED9.anode, LED10.cathode
  N8: M1.pin_1, M4.pin_2, Onderdeel2.B+
  N9: M1.pin_2, M4.pin_1, Onderdeel2.B-
  N10: Powerswitch.L1, VCC1.+
  N11: Powerswitch.COM, Onderdeel2.VMOT
  N12: VCC1.-, Onderdeel2.GND
  GND_2: U1.GND, Onderdeel3.N$92, U2.GND
  N13: U1.pin11, Onderdeel3.N$122, U2.pin11

notes:
  Brake Lights
  Front and backlight
  Turn Left Lights
  Turn Right Lights
  Left Motors
  (Channel B)
  Right Motors
  (Channel A)
  Powersupply
  of some sort
  Left Middle and Right
  Distance sensor IR
  On/Off
